# Fritzing sketch AS_PowerPcb (saved by Fritzing 0.9.3b)
circuit board: 7cm x 3.5cm
breadboards: 1

parts:
  Q3 = npn-Powertransistor [package="TO220 [THT]"]
  Q4 = npn-Powertransistor [package="TO220 [THT]"]
  R1 = Resistor [tolerance=±5% resistance=220 package=THT]
  R2 = Resistor [tolerance=±5% resistance=220 package=THT]
  R3 = Resistor [tolerance=±5% resistance=220 package=THT]
  J4 = longpad pin header, 2 pins [form="long pad"]
  J1 = female pin header, 2 pins [form="♀ (female)"]
  J3 = female pin header, 5 pins [form="♀ (female)"]
  J2 = female pin header, 4 pins [form="♀ (female)"]
  Q5 = npn-Powertransistor [package="TO220 [THT]"]
  R4 = Resistor [tolerance=±5% resistance=220 package=THT]
  Q2 = npn-Powertransistor [package="TO220 [THT]"]
  R5 = Resistor [tolerance=±5% resistance=220 package=THT]

nets:
  N1: Q3.base, R2.Pin_1
  N2: Q3.collector, J3.pin2
  N3: Q3.emitter, Q4.emitter, J4.pin2, J1.pin2, Q5.emitter, Q2.emitter
  N4: Q4.base, R3.Pin_1
  N5: Q4.collector, R5.Pin_1
  N6: R1.Pin_0, J2.pin2
  N7: R1.Pin_1, Q2.base
  N8: R2.Pin_0, J2.pin3
  N9: R3.Pin_0, J2.pin4
  N10: J4.pin1, J1.pin1, J3.pin5
  N11: J3.pin1, R5.Pin_0
  N12: J3.pin3, Q2.collector
  N13: J3.pin4, Q5.collector
  N14: J2.pin1, R4.Pin_0
  N15: Q5.base, R4.Pin_1
