# Fritzing sketch AS_SB (saved by Fritzing 0.9.3b)
circuit board: 12cm x 12cm

parts:
  RGB_Strip_LED7 = RGB Strip LED
  RGB_Strip_LED8 = RGB Strip LED
  R1 = Resistor [tolerance=±5% resistance=220 package=THT]
  J1 = female pin header, 4 pins [form="♀ (female)"]
  LED9 = LED - 5mm [color="Yellow (592nm)" package="5 mm [THT]"]
  LED10 = LED - 5mm [color="Yellow (592nm)" package="5 mm [THT]"]
  LED11 = LED - 5mm [color="Yellow (592nm)" package="5 mm [THT]"]
  R2 = Resistor [tolerance=±5% resistance=220 package=THT]
  LED15 = LED - 5mm [color="Yellow (592nm)" package="5 mm [THT]"]
  RGB_Strip_LED9 = RGB Strip LED
  RGB_Strip_LED10 = RGB Strip LED
  RGB_Strip_LED11 = RGB Strip LED
  RGB_Strip_LED12 = RGB Strip LED
  RGB_Strip_LED13 = RGB Strip LED
  RGB_Strip_LED15 = RGB Strip LED
  RGB_Strip_LED16 = RGB Strip LED
  RGB_Strip_LED17 = RGB Strip LED
  RGB_Strip_LED18 = RGB Strip LED
  RGB_Strip_LED14 = RGB Strip LED
  LED17 = LED - 5mm [color="Yellow (592nm)" package="5 mm [THT]"]
  R3 = Resistor [tolerance=±5% resistance=220 package=THT]
  LED18 = LED - 5mm [color="Yellow (592nm)" package="5 mm [THT]"]
  LED19 = LED - 5mm [color="Yellow (592nm)" package="5 mm [THT]"]
  LED20 = LED - 5mm [color="Yellow (592nm)" package="5 mm [THT]"]
  LED21 = LED - 5mm [color="Yellow (592nm)" package="5 mm [THT]"]
  LED22 = LED - 5mm [color="Yellow (592nm)" package="5 mm [THT]"]
  LED23 = LED - 5mm [color="Yellow (592nm)" package="5 mm [THT]"]
  LED24 = LED - 5mm [color="Yellow (592nm)" package="5 mm [THT]"]
  R4 = Resistor [tolerance=±5% resistance=220 package=THT]
  LED25 = LED - 5mm [color="Yellow (592nm)" package="5 mm [THT]"]
  LED26 = LED - 5mm [color="Yellow (592nm)" package="5 mm [THT]"]
  LED27 = LED - 5mm [color="Yellow (592nm)" package="5 mm [THT]"]
  LED28 = LED - 5mm [color="Yellow (592nm)" package="5 mm [THT]"]
  R5 = Resistor [tolerance=±5% resistance=220 package=THT]
  LED29 = LED - 5mm [color="Yellow (592nm)" package="5 mm [THT]"]
  LED30 = LED - 5mm [color="Yellow (592nm)" package="5 mm [THT]"]
  LED31 = LED - 5mm [color="Yellow (592nm)" package="5 mm [THT]"]
  LED32 = LED - 5mm [color="Yellow (592nm)" package="5 mm [THT]"]
  LED33 = LED - 5mm [color="Yellow (592nm)" package="5 mm [THT]"]
  LED34 = LED - 5mm [color="Yellow (592nm)" package="5 mm [THT]"]
  LED35 = LED - 5mm [color="Yellow (592nm)" package="5 mm [THT]"]
  LED36 = LED - 5mm [color="Yellow (592nm)" package="5 mm [THT]"]
  R6 = Resistor [tolerance=±5% resistance=220 package=THT]
  LED37 = LED - 5mm [color="Yellow (592nm)" package="5 mm [THT]"]
  LED38 = LED - 5mm [color="Yellow (592nm)" package="5 mm [THT]"]
  LED39 = LED - 5mm [color="Yellow (592nm)" package="5 mm [THT]"]
  LED40 = LED - 5mm [color="Yellow (592nm)" package="5 mm [THT]"]
  R7 = Resistor [tolerance=±5% resistance=220 package=THT]
  LED41 = LED - 5mm [color="Yellow (592nm)" package="5 mm [THT]"]
  LED42 = LED - 5mm [color="Yellow (592nm)" package="5 mm [THT]"]
  LED43 = LED - 5mm [color="Yellow (592nm)" package="5 mm [THT]"]
  LED44 = LED - 5mm [color="Yellow (592nm)" package="5 mm [THT]"]
  R8 = Resistor [tolerance=±5% resistance=220 package=THT]
  R9 = Resistor [tolerance=±5% resistance=220 package=THT]
  LED45 = LED - 5mm [color="Yellow (592nm)" package="5 mm [THT]"]
  LED46 = LED - 5mm [color="Yellow (592nm)" package="5 mm [THT]"]
  LED47 = LED - 5mm [color="Yellow (592nm)" package="5 mm [THT]"]
  LED48 = LED - 5mm [color="Yellow (592nm)" package="5 mm [THT]"]
  LED49 = LED - 5mm [color="Yellow (592nm)" package="5 mm [THT]"]
  LED50 = LED - 5mm [color="Yellow (592nm)" package="5 mm [THT]"]
  LED51 = LED - 5mm [color="Yellow (592nm)" package="5 mm [THT]"]
  LED52 = LED - 5mm [color="Yellow (592nm)" package="5 mm [THT]"]
  R10 = Resistor [tolerance=±5% resistance=220 package=THT]
  R11 = Resistor [tolerance=±5% resistance=220 package=THT]
  LED53 = LED - 5mm [color="Yellow (592nm)" package="5 mm [THT]"]
  LED54 = LED - 5mm [color="Yellow (592nm)" package="5 mm [THT]"]
  LED55 = LED - 5mm [color="Yellow (592nm)" package="5 mm [THT]"]
  LED56 = LED - 5mm [color="Yellow (592nm)" package="5 mm [THT]"]
  LED57 = LED - 5mm [color="Yellow (592nm)" package="5 mm [THT]"]
  LED58 = LED - 5mm [color="Yellow (592nm)" package="5 mm [THT]"]
  LED59 = LED - 5mm [color="Yellow (592nm)" package="5 mm [THT]"]
  LED60 = LED - 5mm [color="Yellow (592nm)" package="5 mm [THT]"]
  R12 = Resistor [tolerance=±5% resistance=220 package=THT]

nets:
  N1: RGB_Strip_LED7.+12#8, RGB_Strip_LED8.+12#12
  N2: RGB_Strip_LED7.Green#9, RGB_Strip_LED8.Green#13
  N3: RGB_Strip_LED7.Red#10, RGB_Strip_LED8.Red#14
  N4: RGB_Strip_LED7.+12#12, RGB_Strip_LED8.+12#8, R1.Pin_1, J1.pin1, R2.Pin_0, RGB_Strip_LED9.+12#12, RGB_Strip_LED10.+12#8, RGB_Strip_LED11.+12#12, RGB_Strip_LED12.+12#8, RGB_Strip_LED13.+12#8, RGB_Strip_LED15.+12#12, RGB_Strip_LED16.+12#8, RGB_Strip_LED17.+12#12, RGB_Strip_LED18.+12#8, RGB_Strip_LED14.+12#12, R3.Pin_0, R4.Pin_1, R5.Pin_0, R6.Pin_1, R7.Pin_0, R8.Pin_1, R9.Pin_0, R10.Pin_1, R11.Pin_0, R12.Pin_1
  N5: RGB_Strip_LED7.Green#13, RGB_Strip_LED10.Green#9, RGB_Strip_LED11.Green#13, RGB_Strip_LED13.Green#9, RGB_Strip_LED15.Green#13, RGB_Strip_LED18.Green#9
  N6: RGB_Strip_LED7.Red#14, RGB_Strip_LED10.Red#10, RGB_Strip_LED11.Red#14, RGB_Strip_LED13.Red#10, RGB_Strip_LED15.Red#14, RGB_Strip_LED18.Red#10
  N7: RGB_Strip_LED8.Green#9, J1.pin2, RGB_Strip_LED9.Green#13, RGB_Strip_LED12.Green#9, RGB_Strip_LED16.Green#9, RGB_Strip_LED17.Green#13, RGB_Strip_LED14.Green#13
  N8: RGB_Strip_LED8.Red#10, J1.pin3, RGB_Strip_LED9.Red#14, RGB_Strip_LED12.Red#10, RGB_Strip_LED16.Red#10, RGB_Strip_LED17.Red#14, RGB_Strip_LED14.Red#14
  N9: R1.Pin_0, LED9.anode
  N10: J1.pin4, LED15.cathode, LED19.cathode, LED21.cathode, LED28.cathode, LED32.cathode, LED33.cathode, LED40.cathode, LED41.cathode, LED48.cathode, LED49.cathode, LED56.cathode, LED57.cathode
  N11: LED9.cathode, LED10.anode
  N12: LED10.cathode, LED11.anode
  N13: LED11.cathode, LED15.anode
  N14: R2.Pin_1, LED25.anode
  N15: RGB_Strip_LED9.+12#8, RGB_Strip_LED10.+12#12
  N16: RGB_Strip_LED9.Green#9, RGB_Strip_LED10.Green#13
  N17: RGB_Strip_LED9.Red#10, RGB_Strip_LED10.Red#14
  N18: RGB_Strip_LED11.+12#8, RGB_Strip_LED12.+12#12
  N19: RGB_Strip_LED11.Green#9, RGB_Strip_LED12.Green#13
  N20: RGB_Strip_LED11.Red#10, RGB_Strip_LED12.Red#14
  N21: RGB_Strip_LED13.+12#12, RGB_Strip_LED14.+12#8
  N22: RGB_Strip_LED13.Green#13, RGB_Strip_LED14.Green#9
  N23: RGB_Strip_LED13.Red#14, RGB_Strip_LED14.Red#10
  N24: RGB_Strip_LED15.+12#8, RGB_Strip_LED16.+12#12
  N25: RGB_Strip_LED15.Green#9, RGB_Strip_LED16.Green#13
  N26: RGB_Strip_LED15.Red#10, RGB_Strip_LED16.Red#14
  N27: RGB_Strip_LED17.+12#8, RGB_Strip_LED18.+12#12
  N28: RGB_Strip_LED17.Green#9, RGB_Strip_LED18.Green#13
  N29: RGB_Strip_LED17.Red#10, RGB_Strip_LED18.Red#14
  N30: LED17.cathode, LED18.anode
  N31: LED17.anode, R3.Pin_1
  N32: LED18.cathode, LED20.anode
  N33: LED19.anode, LED20.cathode
  N34: LED21.anode, LED22.cathode
  N35: LED22.anode, LED23.cathode
  N36: LED23.anode, LED24.cathode
  N37: LED24.anode, R4.Pin_0
  N38: LED25.cathode, LED26.anode
  N39: LED26.cathode, LED27.anode
  N40: LED27.cathode, LED28.anode
  N41: R5.Pin_1, LED29.anode
  N42: LED29.cathode, LED30.anode
  N43: LED30.cathode, LED31.anode
  N44: LED31.cathode, LED32.anode
  N45: LED33.anode, LED34.cathode
  N46: LED34.anode, LED35.cathode
  N47: LED35.anode, LED36.cathode
  N48: LED36.anode, R6.Pin_0
  N49: LED37.cathode, LED38.anode
  N50: LED37.anode, R7.Pin_1
  N51: LED38.cathode, LED39.anode
  N52: LED39.cathode, LED40.anode
  N53: LED41.anode, LED42.cathode
  N54: LED42.anode, LED43.cathode
  N55: LED43.anode, LED44.cathode
  N56: LED44.anode, R8.Pin_0
  N57: R9.Pin_1, LED45.anode
  N58: LED45.cathode, LED46.anode
  N59: LED46.cathode, LED47.anode
  N60: LED47.cathode, LED48.anode
  N61: LED49.anode, LED50.cathode
  N62: LED50.anode, LED51.cathode
  N63: LED51.anode, LED52.cathode
  N64: LED52.anode, R10.Pin_0
  N65: R11.Pin_1, LED53.anode
  N66: LED53.cathode, LED54.anode
  N67: LED54.cathode, LED55.anode
  N68: LED55.cathode, LED56.anode
  N69: LED57.anode, LED58.cathode
  N70: LED58.anode, LED59.cathode
  N71: LED59.anode, LED60.cathode
  N72: LED60.anode, R12.Pin_0

custom parts:
  RGB Strip LED: A tri-color Strip LED with red, green and blue. Based on LED SMD 5050 RGB Pin order: common cathode - green - red - blue
