# Fritzing sketch enc (saved by Fritzing 0.9.3b)
circuit board: 10cm x 3.5cm
breadboards: 1

parts:
  D1 = Rectifier Diode [part_number=1N4001 package="300 mil [THT]"]
  J1 = male pin header, 6 pins [form="♂ (male)"]
  D2 = Rectifier Diode [part_number=1N4001 package="300 mil [THT]"]
  D3 = Rectifier Diode [part_number=1N4001 package="300 mil [THT]"]
  D4 = Rectifier Diode [part_number=1N4001 package="300 mil [THT]"]
  D5 = Rectifier Diode [part_number=1N4001 package="300 mil [THT]"]
  D6 = Rectifier Diode [part_number=1N4001 package="300 mil [THT]"]
  D7 = Rectifier Diode [part_number=1N4001 package="300 mil [THT]"]
  D8 = Rectifier Diode [part_number=1N4001 package="300 mil [THT]"]
  D9 = Rectifier Diode [part_number=1N4001 package="300 mil [THT]"]
  RE_SW3 = Rotary Encoder with Switch [package=THT]
  RE_SW2 = Rotary Encoder with Switch [package=THT]
  RE_SW1 = Rotary Encoder with Switch [package=THT]

nets:
  N1: D1.cathode, RE_SW1.SwitchPin2
  N2: D1.anode, J1.pin3, D2.anode, D3.anode
  N3: J1.pin1, D4.anode, D8.anode, D9.anode
  N4: J1.pin2, D5.anode, D6.anode, D7.anode
  N5: J1.pin4, RE_SW1.EncoderPinC, RE_SW1.SwitchPin1
  N6: J1.pin5, RE_SW2.EncoderPinC, RE_SW2.SwitchPin1
  N7: J1.pin6, RE_SW3.EncoderPinC, RE_SW3.SwitchPin1
  N8: D2.cathode, RE_SW2.SwitchPin2
  N9: D3.cathode, RE_SW3.SwitchPin2
  N10: D4.cathode, RE_SW1.EncoderPinA
  N11: D5.cathode, RE_SW1.EncoderPinB
  N12: D6.cathode, RE_SW2.EncoderPinB
  N13: D7.cathode, RE_SW3.EncoderPinB
  N14: D8.cathode, RE_SW2.EncoderPinA
  N15: D9.cathode, RE_SW3.EncoderPinA
